# Fritzing sketch Connections (saved by Fritzing 0.8.7b)

parts:
  7_Segment1 = 7 Segment Display
  Part1 = Arduino Uno (Rev3)

nets:
  N1: 7_Segment1.Segment_G, Part1.D8
  N2: 7_Segment1.Segment_F, Part1.D7
  N3: 7_Segment1.common_anode, Part1.A5/SCL
  N4: 7_Segment1.Segment_E, Part1.D6_PWM
  N5: 7_Segment1.Segment_D, Part1.D5_PWM
  N6: 7_Segment1.Segment_DP, Part1.D9_PWM
  N7: 7_Segment1.Segment_C, Part1.D4
  N8: 7_Segment1.Segment_B, Part1.D3_PWM
  N9: 7_Segment1.Segment_A, Part1.D2
